# Fritzing sketch Devre (saved by Fritzing 0.9.3b)
breadboards: 1

parts:
  IC1 = L293D [package=THT]
  Parça1 = BluePill
  M1 = DC Motor
  U1 = POT [package=pot_mammoth]

nets:
  N1: IC1.Enable_1, Parça1.A0
  N2: IC1.In_1, Parça1.B0
  N3: IC1.Out_1_(_Controlled_by_Enable_1_), M1.pin_2
  GND: IC1.0V, Parça1.GND, Parça1.GND2, Parça1.GND3, U1.S
  N4: IC1.Out_2_(_Controlled_by_Enable_1_), M1.pin_1
  N5: IC1.In_2, Parça1.B1
  N6: IC1.+Vmotor, IC1.+V, Parça1.5V
  N7: Parça1.A1, U1.A
  N8: Parça1.3V3, U1.E

notes:
  USART1 TX
